# Fritzing sketch Seatalk 1 Breadboard sch-v1 (saved by Fritzing 0.9.10b)
breadboards: 2

parts:
  R1 = Resistor [tolerance=±5% power=0.25 resistance=4.7k package=THT]
  R2 = Resistor [tolerance=±5% power=0.25 resistance=39k package=THT]
  R3 = Resistor [tolerance=±5% power=0.25 resistance=15k package=THT]
  R4 = Resistor [tolerance=±5% power=0.25 resistance=27k package=THT]
  R5 = Resistor [tolerance=±5% power=0.25 resistance=6.8k package=THT]
  R6 = Resistor [tolerance=±5% power=0.25 resistance=1k package=THT]
  R7 = Resistor [tolerance=±5% power=0.25 resistance=1k package=THT]
  R8 = Resistor [tolerance=±5% power=0.25 resistance=10 package=THT]
  D1 = Rectifier Diode [part_number=1N4148 package="300 mil [THT]"]
  R9 = Resistor [tolerance=±5% power=0.25 resistance=390 package=THT]
  R10 = Resistor [tolerance=±5% power=0.25 resistance=39k package=THT]
  R11 = Resistor [tolerance=±5% power=0.25 resistance=2.2k package=THT]
  R12 = Resistor [tolerance=±5% power=0.25 resistance=2.2k package=THT]
  R13 = Resistor [tolerance=±5% power=0.25 resistance=10k package=THT]
  C1 = Ceramic Capacitor [capacitance=100nF voltage=35V package="100 mil [THT, multilayer]"]
  R15 = Resistor [tolerance=±5% power=0.25 resistance=2.2k package=THT]
  R16 = Resistor [tolerance=±5% power=0.25 resistance=2.2k package=THT]
  R17 = Resistor [tolerance=±5% power=0.25 resistance=4.7k package=THT]
  D2 = Rectifier Diode [part_number=1N4148 package="300 mil [THT]"]
  L1 = Inductor [inductance=1µH package="400 mil [THT]"]
  L2 = Inductor [inductance=10µH package="400 mil [THT]"]
  C2 = Ceramic Capacitor [capacitance=1pF voltage=35V package="100 mil [THT, multilayer]"]
  L3 = Inductor [inductance=10µH package="400 mil [THT]"]
  L4 = Inductor [inductance=10µH package="400 mil [THT]"]
  C3 = Ceramic Capacitor [capacitance=1µF voltage=35V package="100 mil [THT, multilayer]"]
  C4 = Ceramic Capacitor [capacitance=1µF voltage=35V package="100 mil [THT, multilayer]"]
  D3 = Rectifier Diode [part_number=1N4001 package="300 mil [THT]"]
  C5 = Electrolytic Capacitor [capacitance=330µF voltage=35V package="100 mil [THT, electrolytic]"]
  D4 = Rectifier Diode [part_number=1N4001 package="300 mil [THT]"]
  R18 = Resistor [tolerance=±5% power=0.25 resistance=10 package=THT]
  R19 = Resistor [tolerance=±5% power=0.25 resistance=10 package=THT]
  C6 = Electrolytic Capacitor [capacitance=220µF voltage=35V package="100 mil [THT, electrolytic]"]
  U1 = Voltage Regulator - 5V [package="TO220 [THT]"]
  M1 = DOIT Esp32 DevKit v1 (30 pins long, 11 pins width) [part_number=ESP32S-PIN30]
  R20 = Resistor [tolerance=±5% power=0.25 resistance=220 package=THT]
  R21 = Resistor [tolerance=±5% power=0.25 resistance=220 package=THT]
  LED1 = LED - 5mm [color="Red (633nm)" current=0.030 package="5 mm [THT]"]
  LED2 = LED - 5mm [color="Red (633nm)" current=0.030 package="5 mm [THT]"]
  S1 = Pushbutton [package="[THT]"]
  S2 = Pushbutton [package="[THT]"]
  S3 = Pushbutton [package="[THT]"]
  R22 = Resistor [tolerance=±5% power=0.25 resistance=220 package=THT]
  R23 = Resistor [tolerance=±5% power=0.25 resistance=220 package=THT]
  R24 = Resistor [tolerance=±5% power=0.25 resistance=220 package=THT]
  Q1 = NPN-Transistor [package="TO92 [THT]"]
  Q2 = NPN-Transistor [package="TO92 [THT]"]
  Q3 = NPN-Transistor [package="TO92 [THT]"]
  Q5 = PNP-Transistor [package="TO92 [THT]"]
  Q4 = NPN-Transistor [package="TO92 [THT]"]
  Q6 = NPN-Transistor [package="TO92 [THT]"]
  R14 = Resistor [tolerance=±5% power=0.25 resistance=220 package=THT]

nets:
  GND: R1.Pin_0, R8.Pin_0, C2.0, L4.pin_1, C4.0, C5.-, C6.-, U1.GND, M1.GND, S1.Pin_1, S1.Pin_2, S2.Pin_1, S2.Pin_2, S3.Pin_1, S3.Pin_2, Q1.E, Q2.E, Q4.E, Q6.E
  N1: R1.Pin_1, R2.Pin_0, Q1.B
  N2: R2.Pin_1, R3.Pin_0, D2.anode
  12V: R3.Pin_1, R10.Pin_1, R12.Pin_1, D4.cathode, Q5.E, R14.Pin_1
  N3: R4.Pin_0, Q1.C, Q2.B
  3.3V: R4.Pin_1, R5.Pin_1, R11.Pin_1, R17.Pin_1, M1.3V3, LED1.anode, LED2.anode, R22.Pin_1, R23.Pin_1, R24.Pin_1
  N4: R5.Pin_0, R6.Pin_0, Q2.C
  RXD: R6.Pin_1, M1.D27, M1.D14
  N5: R7.Pin_0, R8.Pin_1, Q3.E
  N6: R7.Pin_1, R16.Pin_0, Q4.B
  N7: D1.cathode, Q3.C
  N8: D1.anode, R9.Pin_0, D2.cathode, L2.pin_1
  N9: R9.Pin_1, R10.Pin_0, Q5.C
  N10: R11.Pin_0, Q3.B, Q4.C
  N11: R12.Pin_0, R13.Pin_1, Q5.B
  N12: R13.Pin_0, C1.1
  N13: C1.0, Q6.C, R14.Pin_0
  N14: R15.Pin_0, Q6.B
  TXD: R15.Pin_1, R16.Pin_1, R17.Pin_0, M1.D12
  Seatalk: L1.pin_0
  N15: L1.pin_1, L2.pin_0, C2.1
  ST12V: L3.pin_0, C3.1
  N16: L3.pin_1, C4.1, D3.anode, D4.anode
  ST0V: L4.pin_0, C3.0
  N17: D3.cathode, R18.Pin_1, R19.Pin_1
  N18: C5.+, R18.Pin_0, R19.Pin_0, U1.input_voltage
  5V: C6.+, U1.output_voltage, M1.VIN
  N19: M1.D5, S2.Pin_3, S2.Pin_4, R24.Pin_0
  N20: M1.D18, S1.Pin_3, S1.Pin_4, R23.Pin_0
  N21: M1.D19, S3.Pin_3, S3.Pin_4, R22.Pin_0
  N22: M1.D25, R20.Pin_0
  N23: M1.D26, R21.Pin_0
  N24: R20.Pin_1, LED2.cathode
  N25: R21.Pin_1, LED1.cathode

notes:
  3.3V from ESP32
  Raymarine Seatalk 1

custom parts:
  DOIT Esp32 DevKit v1 (30 pins long, 11 pins width): The DOIT Esp32 DevKit v1 is one of the development board created by DOIT to evaluate the ESP-WROOM-32 module. It is based on the ESP32 microcontroller that boasts Wifi, Bluetooth, Ethernet and Low Power support all in a single chip. (vanepp) made breadboard work, adjusted pin numbering and labels and reduced size of schematic and cleaned up pcb. This chip is 30pins long (2 x15) and 11 pins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
